// Logisim project cpu.circ as structural Verilog
module sips (
  input  [31:0] in_1
);

  wire and_1_out, and_2_out, or_1_out, undriven;
  wire [2:0] ex_da_1_out_17_2;
  wire [4:0] ex_da_1_out_13, ex_da_1_out_14, if_rr_1_out_13, if_rr_1_out_14, if_rr_1_out_15, if_rr_1_out_16,
       rr_ex_1_out_13, rr_ex_1_out_14, undriven_3;
  wire [5:0] ex_da_1_out_12, if_rr_1_out_12, if_rr_1_out_17, multiplexer_2_out, rr_ex_1_out_12,
       rr_ex_1_out_17;
  wire [5:3] ex_da_1_out_17, rr_ex_1_out_17_2;
  wire [7:0] undriven_5, undriven_6, undriven_7, undriven_8;
  wire [15:0] bit_extender_1_out, ex_da_1_out_18, if_rr_1_out_18, rr_ex_1_out_18, undriven_4;
  wire [25:0] bit_extender_2_out, ex_da_1_out_19, if_rr_1_out_19, rr_ex_1_out_19;
  wire [31:0] alu_1_out_6, bit_extender_3_out, bit_extender_4_out, bit_extender_5_out, bit_extender_6_out,
       bit_extender_7_out, ex_da_1_out_15, ex_da_1_out_16, ex_da_1_out_20, if_rr_1_out_20, multiplexer_1_out,
       multiplexer_3_out, multiplexer_4_out, regs_1_out_6, regs_1_out_7, rr_ex_1_out_15, rr_ex_1_out_16,
       rr_ex_1_out_20, undriven_2;

  Bit_Extender #(.in_width(32), .\type ("zero")) bit_extender_1 (.in(in_1), .out(bit_extender_1_out));
  Bit_Extender #(.in_width(32), .out_width(26), .\type ("zero")) bit_extender_2 (.in(in_1), .out(bit_extender_2_out));
  if_rr if_rr_1 (
    .in_2(in_1[10:6]), .in_3(in_1[15:11]), .in_4(in_1[20:16]), .in_5(in_1[25:21]), .in_6(in_1[31:26]),
    .in_7(bit_extender_1_out), .in_8(bit_extender_2_out), .in_1(in_1[5:0]), .out_13(if_rr_1_out_13),
    .out_14(if_rr_1_out_14), .out_15(if_rr_1_out_15), .out_16(if_rr_1_out_16), .out_17(if_rr_1_out_17),
    .out_18(if_rr_1_out_18), .out_19(if_rr_1_out_19), .out_20(if_rr_1_out_20), .out_12(if_rr_1_out_12));  // open: in_9, in_10, in_11
  Regs regs_1 (
    .in_1(undriven_3), .in_2(if_rr_1_out_15), .in_3(if_rr_1_out_16), .in_4(undriven_2), .in_5(undriven),
    .out_6(regs_1_out_6), .out_7(regs_1_out_7));
  assign bit_extender_3_out = {{16{1'b0}}, if_rr_1_out_18};  // Bit_Extender bit_extender_3
  or or_1 (or_1_out, if_rr_1_out_17[5], if_rr_1_out_17[4], if_rr_1_out_17[3], if_rr_1_out_17[2], if_rr_1_out_17[1], if_rr_1_out_17[0]);
  rr_ex rr_ex_1 (
    .in_2(if_rr_1_out_13), .in_3(if_rr_1_out_14), .in_4(regs_1_out_6), .in_5(multiplexer_1_out),
    .in_6(if_rr_1_out_17), .in_7(if_rr_1_out_18), .in_8(if_rr_1_out_19), .in_9(if_rr_1_out_20),
    .in_1(if_rr_1_out_12), .out_13(rr_ex_1_out_13), .out_14(rr_ex_1_out_14), .out_15(rr_ex_1_out_15),
    .out_16(rr_ex_1_out_16),
    .out_17({rr_ex_1_out_17_2, rr_ex_1_out_17[0], rr_ex_1_out_17[1], rr_ex_1_out_17[2]}),
    .out_18(rr_ex_1_out_18), .out_19(rr_ex_1_out_19), .out_20(rr_ex_1_out_20), .out_12(rr_ex_1_out_12));  // open: in_10, in_11
  Multiplexer #(.width(32)) multiplexer_1 (
    .in0(regs_1_out_7), .in1(bit_extender_3_out), .out(multiplexer_1_out), .sel(or_1_out));
  and and_1 (and_1_out, ~rr_ex_1_out_17_2[5], ~rr_ex_1_out_17_2[4], rr_ex_1_out_17_2[3], rr_ex_1_out_17[0], rr_ex_1_out_17[1], rr_ex_1_out_17[2]);  // AND_Gate
  Pull_Resistor #(.pull(1)) pull_resistor_1 (.node(rr_ex_1_out_17[5]));
  and and_2 (and_2_out, rr_ex_1_out_17_2[5], rr_ex_1_out_17_2[4], ~rr_ex_1_out_17_2[3]);  // AND_Gate
  and and_3 (rr_ex_1_out_17[3], rr_ex_1_out_17[0], ~rr_ex_1_out_17[1]);  // AND_Gate
  Multiplexer #(.width(6)) multiplexer_2 (
    .in0(rr_ex_1_out_12), .in1(rr_ex_1_out_17), .out(multiplexer_2_out), .sel(and_2_out));
  Pull_Resistor pull_resistor_2 (.node(rr_ex_1_out_17[4]));
  alu alu_1 (
    .in_1(rr_ex_1_out_15), .in_2(rr_ex_1_out_16), .in_3(multiplexer_2_out), .in_4(rr_ex_1_out_13),
    .out_6(alu_1_out_6));  // open: out_7, out_8, in_5
  Multiplexer #(.width(32)) multiplexer_3 (
    .in0(alu_1_out_6), .in1({rr_ex_1_out_16[15:0], undriven_4}), .out(multiplexer_3_out), .sel(and_1_out));
  ex_da ex_da_1 (
    .in_2(rr_ex_1_out_13), .in_3(rr_ex_1_out_14), .in_4(multiplexer_3_out), .in_5(rr_ex_1_out_15),
    .in_6({rr_ex_1_out_17_2, rr_ex_1_out_17[0], rr_ex_1_out_17[1], rr_ex_1_out_17[2]}),
    .in_7(rr_ex_1_out_18), .in_8(rr_ex_1_out_19), .in_9(rr_ex_1_out_20), .in_1(rr_ex_1_out_12),
    .out_13(ex_da_1_out_13), .out_14(ex_da_1_out_14), .out_15(ex_da_1_out_15), .out_16(ex_da_1_out_16),
    .out_17({ex_da_1_out_17, ex_da_1_out_17_2}), .out_18(ex_da_1_out_18), .out_19(ex_da_1_out_19),
    .out_20(ex_da_1_out_20), .out_12(ex_da_1_out_12));  // open: in_10, in_11
  assign bit_extender_4_out = {{24{undriven_5[7]}}, undriven_5};  // Bit_Extender bit_extender_4
  assign bit_extender_5_out = {{16{undriven_6[7]}}, {undriven_6, undriven_5}};  // Bit_Extender bit_extender_5
  assign bit_extender_6_out = {{24{1'b0}}, undriven_5};  // Bit_Extender bit_extender_6
  assign bit_extender_7_out = {{16{1'b0}}, {undriven_6, undriven_5}};  // Bit_Extender bit_extender_7
  Multiplexer #(.select(3), .width(32)) multiplexer_4 (
    .in0(bit_extender_4_out), .in1(bit_extender_5_out),
    .in3({undriven_8, undriven_7, undriven_6, undriven_5}), .in4(bit_extender_6_out),
    .in5(bit_extender_7_out), .out(multiplexer_4_out), .sel(ex_da_1_out_17_2));  // open: in2, in6, in7
endmodule

module Regs (
  input  [4:0] in_1,
  input  [4:0] in_2,
  input  [4:0] in_3,
  input  [31:0] in_4,
  input  in_5,
  output [31:0] out_6,
  output [31:0] out_7
);

  wire decoder_1_out1, decoder_1_out2, decoder_1_out3, decoder_1_out4, decoder_1_out5, decoder_1_out6,
       decoder_1_out7, decoder_1_out8, decoder_1_out9, decoder_1_out10, decoder_1_out11, decoder_1_out12,
       decoder_1_out13, decoder_1_out14, decoder_1_out15, decoder_1_out16, decoder_1_out17, decoder_1_out18,
       decoder_1_out19, decoder_1_out20, decoder_1_out21, decoder_1_out22, decoder_1_out23, decoder_1_out24,
       decoder_1_out25, decoder_1_out26, decoder_1_out27, decoder_1_out28, decoder_1_out29, decoder_1_out30,
       decoder_1_out31;
  wire [31:0] pull_resistor_1_node, register_1_q, register_2_q, register_3_q, register_4_q, register_5_q,
       register_6_q, register_7_q, register_8_q, register_9_q, register_10_q, register_11_q, register_12_q,
       register_13_q, register_14_q, register_15_q, register_16_q, register_17_q, register_18_q,
       register_19_q, register_20_q, register_21_q, register_22_q, register_23_q, register_24_q,
       register_25_q, register_26_q, register_27_q, register_28_q, register_29_q, register_30_q,
       register_31_q;

  Decoder #(.select(5)) decoder_1 (
    .out1(decoder_1_out1), .out2(decoder_1_out2), .out3(decoder_1_out3), .out4(decoder_1_out4),
    .out5(decoder_1_out5), .out6(decoder_1_out6), .out7(decoder_1_out7), .out8(decoder_1_out8),
    .out9(decoder_1_out9), .out10(decoder_1_out10), .out11(decoder_1_out11), .out12(decoder_1_out12),
    .out13(decoder_1_out13), .out14(decoder_1_out14), .out15(decoder_1_out15), .out16(decoder_1_out16),
    .out17(decoder_1_out17), .out18(decoder_1_out18), .out19(decoder_1_out19), .out20(decoder_1_out20),
    .out21(decoder_1_out21), .out22(decoder_1_out22), .out23(decoder_1_out23), .out24(decoder_1_out24),
    .out25(decoder_1_out25), .out26(decoder_1_out26), .out27(decoder_1_out27), .out28(decoder_1_out28),
    .out29(decoder_1_out29), .out30(decoder_1_out30), .out31(decoder_1_out31), .sel(in_1), .en(in_5));  // open: out0
  Pull_Resistor pull_resistor_1 (.node(pull_resistor_1_node));
  Register #(.width(32)) register_1 (.D(in_4), .Q(register_1_q), .clk(decoder_1_out1));  // open: en, clr
  Register #(.width(32)) register_2 (.D(in_4), .Q(register_2_q), .clk(decoder_1_out2));  // open: en, clr
  Register #(.width(32)) register_3 (.D(in_4), .Q(register_3_q), .clk(decoder_1_out3));  // open: en, clr
  Register #(.width(32)) register_4 (.D(in_4), .Q(register_4_q), .clk(decoder_1_out4));  // open: en, clr
  Register #(.width(32)) register_5 (.D(in_4), .Q(register_5_q), .clk(decoder_1_out5));  // open: en, clr
  Register #(.width(32)) register_6 (.D(in_4), .Q(register_6_q), .clk(decoder_1_out6));  // open: en, clr
  Register #(.width(32)) register_7 (.D(in_4), .Q(register_7_q), .clk(decoder_1_out7));  // open: en, clr
  Register #(.width(32)) register_8 (.D(in_4), .Q(register_8_q), .clk(decoder_1_out8));  // open: en, clr
  Register #(.width(32)) register_9 (.D(in_4), .Q(register_9_q), .clk(decoder_1_out9));  // open: en, clr
  Register #(.width(32)) register_10 (.D(in_4), .Q(register_10_q), .clk(decoder_1_out10));  // open: en, clr
  Register #(.width(32)) register_11 (.D(in_4), .Q(register_11_q), .clk(decoder_1_out11));  // open: en, clr
  Register #(.width(32)) register_12 (.D(in_4), .Q(register_12_q), .clk(decoder_1_out12));  // open: en, clr
  Register #(.width(32)) register_13 (.D(in_4), .Q(register_13_q), .clk(decoder_1_out13));  // open: en, clr
  Register #(.width(32)) register_14 (.D(in_4), .Q(register_14_q), .clk(decoder_1_out14));  // open: en, clr
  Register #(.width(32)) register_15 (.D(in_4), .Q(register_15_q), .clk(decoder_1_out15));  // open: en, clr
  Register #(.width(32)) register_16 (.D(in_4), .Q(register_16_q), .clk(decoder_1_out16));  // open: en, clr
  Register #(.width(32)) register_17 (.D(in_4), .Q(register_17_q), .clk(decoder_1_out17));  // open: en, clr
  Register #(.width(32)) register_18 (.D(in_4), .Q(register_18_q), .clk(decoder_1_out18));  // open: en, clr
  Register #(.width(32)) register_19 (.D(in_4), .Q(register_19_q), .clk(decoder_1_out19));  // open: en, clr
  Register #(.width(32)) register_20 (.D(in_4), .Q(register_20_q), .clk(decoder_1_out20));  // open: en, clr
  Register #(.width(32)) register_21 (.D(in_4), .Q(register_21_q), .clk(decoder_1_out21));  // open: en, clr
  Register #(.width(32)) register_22 (.D(in_4), .Q(register_22_q), .clk(decoder_1_out22));  // open: en, clr
  Register #(.width(32)) register_23 (.D(in_4), .Q(register_23_q), .clk(decoder_1_out23));  // open: en, clr
  Register #(.width(32)) register_24 (.D(in_4), .Q(register_24_q), .clk(decoder_1_out24));  // open: en, clr
  Register #(.width(32)) register_25 (.D(in_4), .Q(register_25_q), .clk(decoder_1_out25));  // open: en, clr
  Register #(.width(32)) register_26 (.D(in_4), .Q(register_26_q), .clk(decoder_1_out26));  // open: en, clr
  Register #(.width(32)) register_27 (.D(in_4), .Q(register_27_q), .clk(decoder_1_out27));  // open: en, clr
  Register #(.width(32)) register_28 (.D(in_4), .Q(register_28_q), .clk(decoder_1_out28));  // open: en, clr
  Register #(.width(32)) register_29 (.D(in_4), .Q(register_29_q), .clk(decoder_1_out29));  // open: en, clr
  Register #(.width(32)) register_30 (.D(in_4), .Q(register_30_q), .clk(decoder_1_out30));  // open: en, clr
  Register #(.width(32)) register_31 (.D(in_4), .Q(register_31_q), .clk(decoder_1_out31));  // open: en, clr
  Multiplexer #(.select(5), .width(32)) multiplexer_1 (
    .in0(pull_resistor_1_node), .in1(register_1_q), .in2(register_2_q), .in3(register_3_q),
    .in4(register_4_q), .in5(register_5_q), .in6(register_6_q), .in7(register_7_q), .in8(register_8_q),
    .in9(register_9_q), .in10(register_10_q), .in11(register_11_q), .in12(register_12_q),
    .in13(register_13_q), .in14(register_14_q), .in15(register_15_q), .in16(register_16_q),
    .in17(register_17_q), .in18(register_18_q), .in19(register_19_q), .in20(register_20_q),
    .in21(register_21_q), .in22(register_22_q), .in23(register_23_q), .in24(register_24_q),
    .in25(register_25_q), .in26(register_26_q), .in27(register_27_q), .in28(register_28_q),
    .in29(register_29_q), .in30(register_30_q), .in31(register_31_q), .out(out_6), .sel(in_2));
  Multiplexer #(.select(5), .width(32)) multiplexer_2 (
    .in0(pull_resistor_1_node), .in1(register_1_q), .in2(register_2_q), .in3(register_3_q),
    .in4(register_4_q), .in5(register_5_q), .in6(register_6_q), .in7(register_7_q), .in8(register_8_q),
    .in9(register_9_q), .in10(register_10_q), .in11(register_11_q), .in12(register_12_q),
    .in13(register_13_q), .in14(register_14_q), .in15(register_15_q), .in16(register_16_q),
    .in17(register_17_q), .in18(register_18_q), .in19(register_19_q), .in20(register_20_q),
    .in21(register_21_q), .in22(register_22_q), .in23(register_23_q), .in24(register_24_q),
    .in25(register_25_q), .in26(register_26_q), .in27(register_27_q), .in28(register_28_q),
    .in29(register_29_q), .in30(register_30_q), .in31(register_31_q), .out(out_7), .sel(in_3));
endmodule

module alu (
  input  [31:0] in_1,
  input  [31:0] in_2,
  input  [5:0] in_3,
  input  [4:0] in_4,
  input  in_5,
  output [31:0] out_6,
  output out_7,
  output out_8
);

  wire adder_1_cout, and_1_out, and_2_out, and_6_out, and_7_out, and_8_out, and_9_out, and_10_out,
       and_11_out, comparator_1_lt, comparator_2_lt, subtractor_1_bout;
  wire [4:0] bit_extender_1_out, multiplexer_1_out;
  wire [31:0] adder_1_out, and_5_out, bit_extender_2_out, bit_extender_3_out, controlled_buffer_1_out,
       controlled_buffer_2_out, divider_1_out, divider_1_rem, divider_2_out, divider_2_rem, hi_q, lo_q,
       multiplexer_2_out, multiplexer_3_out, multiplexer_4_out, multiplexer_5_out, multiplier_1_cout,
       multiplier_1_out, multiplier_2_cout, multiplier_2_out, nor_1_out, or_1_out, or_2_out, or_3_out,
       pull_resistor_1_node, pull_resistor_2_node, shifter_1_out, shifter_2_out, shifter_3_out,
       subtractor_1_out, xor_1_out;

  and and_1 (and_1_out, ~in_3[0], ~in_3[1], ~in_3[2]);  // AND_Gate
  and and_2 (and_2_out, in_3[0], ~in_3[1], in_3[2]);  // AND_Gate
  and and_3 (out_8, subtractor_1_bout, and_1_out);
  and and_4 (out_7, adder_1_cout, and_2_out);
  Multiplexer #(.width(5)) multiplexer_1 (.in0(in_4), .in1(bit_extender_1_out), .out(multiplexer_1_out), .sel(in_3[2]));
  Bit_Extender #(.in_width(32), .out_width(5)) bit_extender_1 (.in(in_1), .out(bit_extender_1_out));
  Shifter #(.width(32)) shifter_1 (.in(in_2), .\dist (multiplexer_1_out), .out(shifter_1_out));
  Shifter #(.shift("lr"), .width(32)) shifter_2 (.in(in_2), .\dist (multiplexer_1_out), .out(shifter_2_out));
  Shifter #(.shift("ar"), .width(32)) shifter_3 (.in(in_2), .\dist (multiplexer_1_out), .out(shifter_3_out));
  Multiplier #(.mode("twosComplement"), .width(32)) multiplier_1 (
    .a(in_1), .b(in_2), .out(multiplier_1_out), .cout(multiplier_1_cout));  // open: cin
  Divider #(.mode("twosComplement"), .width(32)) divider_1 (
    .a(in_1), .b(in_2), .out(divider_1_out), .rem(divider_1_rem));  // open: upper
  Multiplier #(.width(32)) multiplier_2 (
    .a(in_1), .b(in_2), .out(multiplier_2_out), .cout(multiplier_2_cout));  // open: cin
  Divider #(.width(32)) divider_2 (.a(in_1), .b(in_2), .out(divider_2_out), .rem(divider_2_rem));  // open: upper
  Adder #(.width(32)) adder_1 (.a(in_1), .b(in_2), .out(adder_1_out), .cout(adder_1_cout));  // open: cin
  Subtractor #(.width(32)) subtractor_1 (
    .a(in_1), .b(in_2), .out(subtractor_1_out), .bout(subtractor_1_bout));  // open: bin
  assign and_5_out = in_1 & in_2;  // AND_Gate and_5, 32 bits wide
  assign or_1_out = in_1 | in_2;  // OR_Gate or_1, 32 bits wide
  assign xor_1_out = in_1 ^ in_2;  // XOR_Gate xor_1, 32 bits wide
  assign nor_1_out = ~(in_1 | in_2);  // NOR_Gate nor_1, 32 bits wide
  Comparator #(.width(32)) comparator_1 (.a(in_1), .b(in_2), .lt(comparator_1_lt));  // open: gt, eq
  Comparator #(.mode("unsigned"), .width(32)) comparator_2 (.a(in_1), .b(in_2), .lt(comparator_2_lt));  // open: gt, eq
  Multiplexer #(.select(2), .width(32)) multiplexer_2 (
    .in0(shifter_1_out), .in2(shifter_2_out), .in3(shifter_3_out), .out(multiplexer_2_out), .sel(in_3[1:0]));  // open: in1
  Multiplexer #(.select(2), .width(32)) multiplexer_3 (
    .in0(multiplier_1_out), .in1(divider_1_out), .in2(multiplier_2_out), .in3(divider_2_out),
    .out(multiplexer_3_out), .sel(in_3[1:0]));
  Multiplexer #(.select(2), .width(32)) multiplexer_4 (
    .in0(multiplier_1_cout), .in1(divider_1_rem), .in2(multiplier_2_cout), .in3(divider_2_rem),
    .out(multiplexer_4_out), .sel(in_3[1:0]));
  Multiplexer #(.select(3), .width(32)) multiplexer_5 (
    .in0(adder_1_out), .in1(adder_1_out), .in2(subtractor_1_out), .in3(subtractor_1_out), .in4(and_5_out),
    .in5(or_1_out), .in6(xor_1_out), .in7(nor_1_out), .out(multiplexer_5_out), .sel(in_3[2:0]));
  and and_6 (and_6_out, ~in_3[2], in_3[1], ~in_3[0]);  // AND_Gate
  assign bit_extender_2_out = {{31{1'b0}}, comparator_1_lt};  // Bit_Extender bit_extender_2
  assign bit_extender_3_out = {{31{1'b0}}, comparator_2_lt};  // Bit_Extender bit_extender_3
  and and_7 (and_7_out, and_8_out, in_5);
  and and_8 (and_8_out, ~in_3[5], in_3[4], in_3[3]);  // AND_Gate
  and and_9 (and_9_out, ~in_3[2], in_3[1], in_3[0]);  // AND_Gate
  assign controlled_buffer_1_out = and_6_out ? bit_extender_2_out : 32'bz;  // Controlled_Buffer controlled_buffer_1
  assign controlled_buffer_2_out = and_9_out ? bit_extender_3_out : 32'bz;  // Controlled_Buffer controlled_buffer_2
  Pull_Resistor pull_resistor_1 (.node(pull_resistor_1_node));
  assign pull_resistor_1_node = and_11_out ? lo_q : 32'bz;  // Controlled_Buffer controlled_buffer_3
  Register #(.trigger("falling"), .width(32)) lo (.D(multiplexer_3_out), .Q(lo_q), .clk(and_7_out));  // open: en, clr
  Pull_Resistor pull_resistor_2 (.node(pull_resistor_2_node));
  assign pull_resistor_2_node = and_10_out ? hi_q : 32'bz;  // Controlled_Buffer controlled_buffer_4
  Register #(.trigger("falling"), .width(32)) hi (.D(multiplexer_4_out), .Q(hi_q), .clk(and_7_out));  // open: en, clr
  and and_10 (and_10_out, ~in_3[2], ~in_3[1], ~in_3[0]);  // AND_Gate
  and and_11 (and_11_out, ~in_3[2], in_3[1], ~in_3[0]);  // AND_Gate
  Pull_Resistor pull_resistor_3 (.node(controlled_buffer_1_out));
  assign or_2_out = controlled_buffer_1_out | controlled_buffer_2_out;  // OR_Gate or_2, 32 bits wide
  Pull_Resistor pull_resistor_4 (.node(controlled_buffer_2_out));
  assign or_3_out = pull_resistor_1_node | pull_resistor_2_node;  // OR_Gate or_3, 32 bits wide
  Multiplexer #(.select(3), .width(32)) multiplexer_6 (
    .in0(multiplexer_2_out), .in2(or_3_out), .in4(multiplexer_5_out), .in5(or_2_out), .out(out_6),
    .sel(in_3[5:3]));  // open: in1, in3, in6, in7
endmodule

module if_rr (
  input  [5:0] in_1,
  input  [4:0] in_2,
  input  [4:0] in_3,
  input  [4:0] in_4,
  input  [4:0] in_5,
  input  [5:0] in_6,
  input  [15:0] in_7,
  input  [25:0] in_8,
  input  [31:0] in_9,
  input  in_10,
  input  in_11,
  output [5:0] out_12,
  output [4:0] out_13,
  output [4:0] out_14,
  output [4:0] out_15,
  output [4:0] out_16,
  output [5:0] out_17,
  output [15:0] out_18,
  output [25:0] out_19,
  output [31:0] out_20
);

  Register #(.trigger("falling"), .width(6)) register_1 (.D(in_1), .Q(out_12), .clk(in_10), .clr(in_11));  // open: en
  Register #(.trigger("falling"), .width(5)) register_2 (.D(in_2), .Q(out_13), .clk(in_10), .clr(in_11));  // open: en
  Register #(.trigger("falling"), .width(5)) register_3 (.D(in_3), .Q(out_14), .clk(in_10), .clr(in_11));  // open: en
  Register #(.trigger("falling"), .width(5)) register_4 (.D(in_4), .Q(out_15), .clk(in_10), .clr(in_11));  // open: en
  Register #(.trigger("falling"), .width(5)) register_5 (.D(in_5), .Q(out_16), .clk(in_10), .clr(in_11));  // open: en
  Register #(.trigger("falling"), .width(6)) register_6 (.D(in_6), .Q(out_17), .clk(in_10), .clr(in_11));  // open: en
  Register #(.trigger("falling"), .width(16)) register_7 (.D(in_7), .Q(out_18), .clk(in_10), .clr(in_11));  // open: en
  Register #(.trigger("falling"), .width(26)) register_8 (.D(in_8), .Q(out_19), .clk(in_10), .clr(in_11));  // open: en
  Register #(.trigger("falling"), .width(32)) register_9 (.D(in_9), .Q(out_20), .clk(in_10), .clr(in_11));  // open: en
endmodule

module rr_ex (
  input  [5:0] in_1,
  input  [4:0] in_2,
  input  [4:0] in_3,
  input  [31:0] in_4,
  input  [31:0] in_5,
  input  [5:0] in_6,
  input  [15:0] in_7,
  input  [25:0] in_8,
  input  [31:0] in_9,
  input  in_10,
  input  in_11,
  output [5:0] out_12,
  output [4:0] out_13,
  output [4:0] out_14,
  output [31:0] out_15,
  output [31:0] out_16,
  output [5:0] out_17,
  output [15:0] out_18,
  output [25:0] out_19,
  output [31:0] out_20
);

  Register #(.trigger("falling"), .width(6)) register_1 (.D(in_1), .Q(out_12), .clk(in_10), .clr(in_11));  // open: en
  Register #(.trigger("falling"), .width(5)) register_2 (.D(in_2), .Q(out_13), .clk(in_10), .clr(in_11));  // open: en
  Register #(.trigger("falling"), .width(5)) register_3 (.D(in_3), .Q(out_14), .clk(in_10), .clr(in_11));  // open: en
  Register #(.trigger("falling"), .width(32)) register_4 (.D(in_4), .Q(out_15), .clk(in_10), .clr(in_11));  // open: en
  Register #(.trigger("falling"), .width(32)) register_5 (.D(in_5), .Q(out_16), .clk(in_10), .clr(in_11));  // open: en
  Register #(.trigger("falling"), .width(6)) register_6 (.D(in_6), .Q(out_17), .clk(in_10), .clr(in_11));  // open: en
  Register #(.trigger("falling"), .width(16)) register_7 (.D(in_7), .Q(out_18), .clk(in_10), .clr(in_11));  // open: en
  Register #(.trigger("falling"), .width(26)) register_8 (.D(in_8), .Q(out_19), .clk(in_10), .clr(in_11));  // open: en
  Register #(.trigger("falling"), .width(32)) register_9 (.D(in_9), .Q(out_20), .clk(in_10), .clr(in_11));  // open: en
endmodule

module ex_da (
  input  [5:0] in_1,
  input  [4:0] in_2,
  input  [4:0] in_3,
  input  [31:0] in_4,
  input  [31:0] in_5,
  input  [5:0] in_6,
  input  [15:0] in_7,
  input  [25:0] in_8,
  input  [31:0] in_9,
  input  in_10,
  input  in_11,
  output [5:0] out_12,
  output [4:0] out_13,
  output [4:0] out_14,
  output [31:0] out_15,
  output [31:0] out_16,
  output [5:0] out_17,
  output [15:0] out_18,
  output [25:0] out_19,
  output [31:0] out_20
);

  Register #(.trigger("falling"), .width(6)) register_1 (.D(in_1), .Q(out_12), .clk(in_10), .clr(in_11));  // open: en
  Register #(.trigger("falling"), .width(5)) register_2 (.D(in_2), .Q(out_13), .clk(in_10), .clr(in_11));  // open: en
  Register #(.trigger("falling"), .width(5)) register_3 (.D(in_3), .Q(out_14), .clk(in_10), .clr(in_11));  // open: en
  Register #(.trigger("falling"), .width(32)) register_4 (.D(in_4), .Q(out_15), .clk(in_10), .clr(in_11));  // open: en
  Register #(.trigger("falling"), .width(32)) register_5 (.D(in_5), .Q(out_16), .clk(in_10), .clr(in_11));  // open: en
  Register #(.trigger("falling"), .width(6)) register_6 (.D(in_6), .Q(out_17), .clk(in_10), .clr(in_11));  // open: en
  Register #(.trigger("falling"), .width(16)) register_7 (.D(in_7), .Q(out_18), .clk(in_10), .clr(in_11));  // open: en
  Register #(.trigger("falling"), .width(26)) register_8 (.D(in_8), .Q(out_19), .clk(in_10), .clr(in_11));  // open: en
  Register #(.trigger("falling"), .width(32)) register_9 (.D(in_9), .Q(out_20), .clk(in_10), .clr(in_11));  // open: en
endmodule

module idk (
  input  [5:0] in_1,
  input  [4:0] in_2,
  input  [4:0] in_3,
  input  [4:0] in_4,
  input  [4:0] in_5,
  input  [5:0] in_6
);

  // Probe on in_6
  // Probe on {in_6, in_5, in_4, in_3, in_2, in_1}
endmodule
